// Digital circuit ADD_Sel.dig as structural Verilog
module ADD_Sel (
  input  A,
  input  B,
  input  C,
  input  D,
  output Y
);

  wire not_1_out, not_2_out;

  not not_1 (not_1_out, B);
  not not_2 (not_2_out, C);
  and and_1 (Y, A, not_1_out, not_2_out, D);
endmodule
