// Digital circuit AND_Sel.dig as structural Verilog
module AND_Sel (
  input  A,
  input  B,
  input  C,
  input  D,
  output Y
);

  wire not_1_out;

  not not_1 (not_1_out, B);
  and and_1 (Y, A, not_1_out, C, D);
endmodule
