// Digital circuit Control_Unit.dig as structural Verilog
module Control_Unit (
  input  A,
  input  B,
  input  C,
  input  D,
  output RR1,
  output RR2,
  output WR,
  output WE,
  output ADD,
  output SUB,
  output AND,
  output OR,
  output XOR,
  output SLT,
  output IL
);

  RR1 u_RR1 (.A(A), .Y(RR1));
  RR2 u_RR2 (.Y(RR2));
  WR u_WR (.A(A), .B(B), .C(C), .D(D), .Y(WR));
  WE u_WE (.A(A), .C(C), .D(D), .Y(WE));
  ADD_Sel u_ADD (.A(A), .B(B), .C(C), .D(D), .Y(ADD));
  SUB_Sel u_SUB (.A(A), .B(B), .C(C), .D(D), .Y(SUB));
  AND_Sel u_AND (.A(A), .B(B), .C(C), .D(D), .Y(AND));
  OR_Sel u_OR (.A(A), .B(B), .C(C), .D(D), .Y(OR));
  XOR_Sel u_XOR (.A(A), .B(B), .C(C), .D(D), .Y(XOR));
  SLT_Sel u_SLT (.A(A), .B(B), .C(C), .D(D), .Y(SLT));
  IL u_IL (.A(A), .C(C), .D(D), .Y(IL));
endmodule
