// Digital circuit FDE_Cycle.dig as structural Verilog
module FDE_Cycle (
  input  CLK,
  input  IN,
  output [1:0] State
);

  wire and_1_out, and_2_out, and_3_out, and_4_out, not_1_out, not_2_out, not_3_out, not_4_out, or_1_out,
       or_2_out;

  not not_1 (not_1_out, IN);
  not not_2 (not_2_out, IN);
  and and_1 (and_1_out, State[1], not_1_out);
  and and_2 (and_2_out, State[0], IN);
  and and_3 (and_3_out, not_3_out, not_4_out, IN);
  and and_4 (and_4_out, State[0], not_2_out);
  not not_3 (not_3_out, State[1]);
  or or_1 (or_1_out, and_1_out, and_2_out);
  or or_2 (or_2_out, and_3_out, and_4_out);
  not not_4 (not_4_out, State[0]);
  D_FF d_ff_1 (.D(or_1_out), .C(CLK), .Q(State[1]));  // open: nQ
  D_FF d_ff_2 (.D(or_2_out), .C(CLK), .Q(State[0]));  // open: nQ
endmodule
