// Digital circuit IL.dig as structural Verilog
module IL (
  input  A,
  input  C,
  input  D,
  output Y
);

  wire and_1_out, and_2_out, not_1_out;

  not not_1 (not_1_out, A);
  and and_1 (and_1_out, not_1_out, D);
  and and_2 (and_2_out, not_1_out, C);
  or or_1 (Y, and_1_out, and_2_out);
endmodule
