// Digital circuit SLT_Sel.dig as structural Verilog
module SLT_Sel (
  input  A,
  input  B,
  input  C,
  input  D,
  output Y
);

  wire not_1_out;

  not not_1 (not_1_out, D);
  and and_1 (Y, A, B, C, not_1_out);
endmodule
