// Digital circuit XOR_Sel.dig as structural Verilog
module XOR_Sel (
  input  A,
  input  B,
  input  C,
  input  D,
  output Y
);

  wire not_1_out;

  not not_1 (not_1_out, C);
  and and_1 (Y, A, B, not_1_out, D);
endmodule
